// Logisim project ALU.circ as structural Verilog: 16 circuits, main circuit checker
module simple_adder (
  input  A,
  input  B,
  output S,
  output Cout
);

  xor xor_1 (S, A, B);
  and and_1 (Cout, A, B);
endmodule

module full_adder (
  input  Cin,
  input  A,
  input  B,
  output S,
  output Cout
);

  wire simple_adder_1_cout, simple_adder_2_cout, simple_adder_2_s;

  simple_adder simple_adder_1 (.A(Cin), .B(simple_adder_2_s), .S(S), .Cout(simple_adder_1_cout));
  simple_adder simple_adder_2 (.A(A), .B(B), .S(simple_adder_2_s), .Cout(simple_adder_2_cout));
  or or_1 (Cout, simple_adder_1_cout, simple_adder_2_cout);
endmodule

module adder_4bits (
  input  Cin,
  input  [3:0] A,
  input  [3:0] B,
  output [3:0] S,
  output Cout
);

  wire full_adder_1_cout, full_adder_2_cout, full_adder_3_cout;

  full_adder full_adder_1 (.Cin(Cin), .A(A[0]), .B(B[0]), .S(S[0]), .Cout(full_adder_1_cout));
  full_adder full_adder_2 (.Cin(full_adder_1_cout), .A(A[1]), .B(B[1]), .S(S[1]), .Cout(full_adder_2_cout));
  full_adder full_adder_3 (.Cin(full_adder_2_cout), .A(A[2]), .B(B[2]), .S(S[2]), .Cout(full_adder_3_cout));
  full_adder full_adder_4 (.Cin(full_adder_3_cout), .A(A[3]), .B(B[3]), .S(S[3]), .Cout(Cout));
  Hex_Digit_Display hex_digit_display_1 (.value(S));  // open: dp
endmodule

module zero_comparator (
  input  [3:0] A,
  output Z
);

  wire or_1_out, or_2_out;

  or or_1 (or_1_out, A[0], A[1]);
  or or_2 (or_2_out, A[2], A[3]);
  nor nor_1 (Z, or_1_out, or_2_out);
endmodule

module adder_with_flags (
  input  Cin,
  input  [3:0] A,
  input  [3:0] B,
  output [3:0] S,
  output N,
  output Z,
  output V,
  output C
);

  adder_4bits adder_4bits_1 (.Cin(Cin), .A(A), .B(B), .S({N, S[2:0]}), .Cout(C));
  Hex_Digit_Display hex_digit_display_1 (.value({N, S[2:0]}));  // open: dp
  zero_comparator zero_comparator_1 (.A({N, S[2:0]}), .Z(Z));
  overflow_comparator overflow_comparator_1 (.c3(N), .a3(A[3]), .b3(B[3]), .O(V));

  assign S[3] = N;
endmodule

module increaser_4bit (
  input  [3:0] A,
  output [3:0] S
);

  adder_4bits adder_4bits_1 (.A(A), .B(4'b0001), .S(S));  // open: Cin, Cout
  Hex_Digit_Display hex_digit_display_1 (.value(S));  // open: dp
endmodule

module inverter_4bit (
  input  [3:0] A,
  input  INV,
  output [3:0] S
);

  wire [3:0] increaser_4bit_1_s, not_1_out;

  not not_1 (not_1_out[0], A[0]);
  not not_2 (not_1_out[1], A[1]);
  not not_3 (not_1_out[2], A[2]);
  not not_4 (not_1_out[3], A[3]);
  Multiplexer #(.width(4)) multiplexer_1 (.in0(A), .in1(increaser_4bit_1_s), .out(S), .sel(INV));
  increaser_4bit increaser_4bit_1 (.A(not_1_out), .S(increaser_4bit_1_s));
  Hex_Digit_Display hex_digit_display_1 (.value(S));  // open: dp
endmodule

module ALU (
  input  [3:0] A,
  input  [3:0] B,
  input  [1:0] OP,
  output N,
  output Z,
  output V,
  output C,
  output [3:0] S
);

  wire adder_with_flags_1_c, adder_with_flags_1_v, and_1_out, subtraction_carry_1_c_out,
       subtraction_overflow_1_v_out;
  wire [3:0] adder_with_flags_1_s, and_4bits_flags_1_s, inverter_4bit_1_s, or_4bits_flags_1_s;

  and and_1 (and_1_out, OP[0], ~OP[1]);  // AND_Gate
  inverter_4bit inverter_4bit_1 (.A(B), .INV(and_1_out), .S(inverter_4bit_1_s));
  adder_with_flags adder_with_flags_1 (
    .A(A), .B(inverter_4bit_1_s), .S(adder_with_flags_1_s), .V(adder_with_flags_1_v), .C(adder_with_flags_1_c));  // open: Cin, N, Z
  subtraction_overflow subtraction_overflow_1 (
    .V_in(adder_with_flags_1_v), .B(B), .V_out(subtraction_overflow_1_v_out));
  subtraction_carry subtraction_carry_1 (.C_in(adder_with_flags_1_c), .B(B), .C_out(subtraction_carry_1_c_out));
  AND_4bits_flags and_4bits_flags_1 (.A(A), .B(B), .S(and_4bits_flags_1_s));  // open: N, Z
  OR_4bits_flags or_4bits_flags_1 (.A(A), .B(B), .S(or_4bits_flags_1_s));  // open: N, Z
  Multiplexer #(.select(2), .width(4)) multiplexer_1 (
    .in0(adder_with_flags_1_s), .in1(adder_with_flags_1_s), .in2(and_4bits_flags_1_s),
    .in3(or_4bits_flags_1_s), .out({N, S[2:0]}), .sel(OP));
  Hex_Digit_Display hex_digit_display_1 (.value({N, S[2:0]}));  // open: dp
  Multiplexer #(.select(2)) multiplexer_2 (
    .in0(adder_with_flags_1_v), .in1(subtraction_overflow_1_v_out), .in2(1'b0), .in3(1'b0), .out(V), .sel(OP));
  zero_comparator zero_comparator_1 (.A({N, S[2:0]}), .Z(Z));
  Multiplexer #(.select(2)) multiplexer_3 (
    .in0(adder_with_flags_1_c), .in1(subtraction_carry_1_c_out), .in2(1'b0), .in3(1'b0), .out(C), .sel(OP));

  assign S[3] = N;
endmodule

module \checker  (
  output [3:0] out_1,
  output [3:0] out_2,
  output [1:0] out_3,
  output halt,
  output N,
  output Z,
  output V,
  output C,
  output [3:0] res
);

  wire clock_1_out;

  Clock clock_1 (.out(clock_1_out));
  Counter #(.max('h3ff), .width(10)) counter_1 (
    .clk(clock_1_out), .carry(halt), .Q({out_3, out_2, out_1}));  // open: clr, load, up, count, D
  ALU alu_1 (.A(out_1), .B(out_2), .OP(out_3), .N(N), .Z(Z), .V(V), .C(C), .S(res));
endmodule

module subtraction_overflow (
  input  V_in,
  input  [3:0] B,
  output V_out
);

  wire not_2_out, zero_comparator_1_z;
  wire [3:3] not_1_out;

  not not_1 (not_1_out[3], B[3]);
  not not_2 (not_2_out, V_in);
  zero_comparator zero_comparator_1 (.A({not_1_out[3], B[2:0]}), .Z(zero_comparator_1_z));
  Multiplexer multiplexer_1 (.in0(V_in), .in1(not_2_out), .out(V_out), .sel(zero_comparator_1_z));
endmodule

module overflow_comparator (
  input  c3,
  input  a3,
  input  b3,
  output O
);

  wire not_1_out, xor_1_out, xor_2_out;

  xor xor_1 (xor_1_out, c3, a3);
  not not_1 (not_1_out, xor_2_out);
  xor xor_2 (xor_2_out, a3, b3);
  and and_1 (O, xor_1_out, not_1_out);
endmodule

module subtraction_carry (
  input  C_in,
  input  [3:0] B,
  output C_out
);

  wire not_1_out, zero_comparator_1_z;

  not not_1 (not_1_out, C_in);
  Multiplexer multiplexer_1 (.in0(not_1_out), .in1(1'b0), .out(C_out), .sel(zero_comparator_1_z));
  zero_comparator zero_comparator_1 (.A(B), .Z(zero_comparator_1_z));
endmodule

module AND_4bits (
  input  [3:0] A,
  input  [3:0] B,
  output [3:0] S
);

  and and_1 (S[0], A[0], B[0]);
  and and_2 (S[1], A[1], B[1]);
  and and_3 (S[2], A[2], B[2]);
  and and_4 (S[3], A[3], B[3]);
endmodule

module OR_4bits (
  input  [3:0] A,
  input  [3:0] B,
  output [3:0] S
);

  or or_1 (S[0], A[0], B[0]);
  or or_2 (S[1], A[1], B[1]);
  or or_3 (S[2], A[2], B[2]);
  or or_4 (S[3], A[3], B[3]);
endmodule

module AND_4bits_flags (
  input  [3:0] A,
  input  [3:0] B,
  output [3:0] S,
  output N,
  output Z
);

  AND_4bits and_4bits_1 (.A(A), .B(B), .S({N, S[2:0]}));
  zero_comparator zero_comparator_1 (.A({N, S[2:0]}), .Z(Z));

  assign S[3] = N;
endmodule

module OR_4bits_flags (
  input  [3:0] A,
  input  [3:0] B,
  output [3:0] S,
  output N,
  output Z
);

  OR_4bits or_4bits_1 (.A(A), .B(B), .S({N, S[2:0]}));
  zero_comparator zero_comparator_1 (.A({N, S[2:0]}), .Z(Z));

  assign S[3] = N;
endmodule
